# Fritzing sketch Christmas Lights (saved by Fritzing 0.9.3b)
breadboards: 1

parts:
  R1 = Resistor [tolerance=±1% resistance=100 package=THT]
  R5 = Resistor [tolerance=±1% resistance=1k package=THT]
  Arduino_UNO_R3 = Arduino Uno (Rev3)
  Q1 = NPN-Transistor [package="TO92 [THT]"]
  LED1 = LED - 5mm [color="Red (633nm)" package="5 mm [THT]"]
  LED2 = LED - 5mm [color="Red (633nm)" package="5 mm [THT]"]
  LED3 = LED - 5mm [color="Red (633nm)" package="5 mm [THT]"]
  LED4 = LED - 5mm [color="Red (633nm)" package="5 mm [THT]"]
  LED5 = LED - 5mm [color="Red (633nm)" package="5 mm [THT]"]
  LED6 = LED - 5mm [color="Red (633nm)" package="5 mm [THT]"]
  R2 = Resistor [tolerance=±1% resistance=100 package=THT]
  R3 = Resistor [tolerance=±1% resistance=100 package=THT]
  R4 = Resistor [tolerance=±1% resistance=100 package=THT]

nets:
  N1: R1.Pin_0, Q1.C, R2.Pin_0, R3.Pin_0, R4.Pin_0
  N2: R1.Pin_1, LED6.cathode, R2.Pin_1, R3.Pin_1, R4.Pin_1
  N3: R5.Pin_0, Arduino_UNO_R3.D9_PWM
  N4: R5.Pin_1, Q1.B
  GND: Arduino_UNO_R3.GND, Q1.E
  N5: Arduino_UNO_R3.VIN, LED1.anode
  N6: LED1.cathode, LED2.anode
  N7: LED2.cathode, LED3.anode
  N8: LED3.cathode, LED4.anode
  N9: LED4.cathode, LED5.anode
  N10: LED5.cathode, LED6.anode

notes:
  Morse Code Christmas Lights, Drawn By: Courtney Pitcher (igniparoustempest.github.io), 1.0
